// Logisim project 1-bit_adder.circ as structural Verilog
module _2_bitArithmetic (
  input  Cin,
  input  S0,
  input  S1,
  input  [1:0] A_i,
  input  [1:0] B_i,
  output D_i,
  output C_i_2
);

  wire n1_bit_arithmetic_1_c_i_1;

  _1_bit_Arithmetic u_1_bit_arithmetic_1 (
    .Cin(Cin), .S0(S0), .S1(S1), .A_i(A_i[0]), .B_i(B_i[0]), .D_i(D_i), .C_i_1(n1_bit_arithmetic_1_c_i_1));
  _1_bit_Arithmetic u_1_bit_arithmetic_2 (
    .Cin(n1_bit_arithmetic_1_c_i_1), .S0(S0), .S1(S1), .A_i(A_i[1]), .B_i(B_i[1]), .C_i_1(C_i_2));  // open: D_i
endmodule

module _1_bit_Logic (
  input  [1:0] S1_S0,
  input  A_i,
  input  B_i,
  output F_i
);

  wire and_1_out, not_1_out, or_1_out, xor_1_out;

  and and_1 (and_1_out, A_i, B_i);
  or or_1 (or_1_out, A_i, B_i);
  xor xor_1 (xor_1_out, A_i, B_i);
  not not_1 (not_1_out, A_i);
  Multiplexer #(.select(2)) multiplexer_1 (
    .in0(and_1_out), .in1(or_1_out), .in2(xor_1_out), .in3(not_1_out), .out(F_i), .sel(S1_S0));  // open: en
endmodule

module _2_bit_Logic (
  input  [1:0] S1_S0,
  input  [1:0] A,
  input  [1:0] B,
  output F_i,
  output F_i_1
);

  _1_bit_Logic u_1_bit_logic_1 (.S1_S0(S1_S0), .A_i(A[0]), .B_i(B[0]), .F_i(F_i));
  _1_bit_Logic u_1_bit_logic_2 (.S1_S0(S1_S0), .A_i(A[1]), .B_i(B[1]), .F_i(F_i_1));
endmodule

module ALSU (
);

  ProgramCounter programcounter_1 ();
endmodule

module _1_bit_Arithmetic (
  input  Cin,
  input  S0,
  input  S1,
  input  A_i,
  input  B_i,
  output D_i,
  output C_i_1
);

  wire multiplexer_1_out, not_1_out, not_2_out;

  not not_1 (not_1_out, B_i);
  not not_2 (not_2_out, 1'b0);
  Multiplexer #(.select(2)) multiplexer_1 (
    .in0(B_i), .in1(not_1_out), .in2(1'b0), .in3(not_2_out), .out(multiplexer_1_out), .sel({S1, S0}));  // open: en
  Adder #(.width(1)) adder_1 (.a(A_i), .b(multiplexer_1_out), .out(D_i), .cin(Cin), .cout(C_i_1));
endmodule

module ProgramCounter (
);

  wire clock_1_out, controlunit_1_p2, controlunit_1_p3;
  wire [3:0] adder_1_out, controlled_buffer_1_out, register_1_q;

  Clock clock_1 (.out(clock_1_out));
  // ControlUnit controlunit_1: pin names not known; wires that end beside it: clock_1_out, controlunit_1_p2, controlunit_1_p3
  Register #(.width(4)) register_1 (
    .D(adder_1_out), .en(controlunit_1_p2), .Q(register_1_q), .clk(clock_1_out));  // open: clr
  assign controlled_buffer_1_out = controlunit_1_p3 ? register_1_q : 4'bz;  // Controlled_Buffer controlled_buffer_1
  Adder #(.width(4)) adder_1 (.a(register_1_q), .b(4'b0001), .out(adder_1_out));  // open: cin, cout
  // AR_control_main main_1: pin names not known
  Hex_Digit_Display hex_digit_display_1 (.value(register_1_q));  // open: dp
  Hex_Digit_Display hex_digit_display_2 (.value(controlled_buffer_1_out));  // open: dp
  Multiplexer multiplexer_1 ();  // open: in0, in1, out, sel, en
endmodule

module ControlUnit (
  input  clk_in,
  input  [2:0] Op_code,
  input  Mode,
  output T0,
  output T1,
  output T2,
  output T3,
  output T4,
  output T5,
  output T6,
  output D0,
  output D1,
  output D2,
  output D3,
  output D4,
  output D5,
  output D6,
  output D7
);

  wire [2:0] counter_1_q;

  Decoder #(.select(3)) decoder_1 (
    .out0(D0), .out1(D1), .out2(D2), .out3(D3), .out4(D4), .out5(D5), .out6(D6), .out7(D7), .sel(Op_code));  // open: en
  Counter #(.width(3), .max('h5)) counter_1 (.Q(counter_1_q), .clk(clk_in));  // open: load, D, count, carry, clr
  Decoder #(.select(3)) decoder_2 (
    .out0(T0), .out1(T1), .out2(T2), .out3(T3), .out4(T4), .out5(T5), .out6(T6), .sel(counter_1_q));  // open: out7, en
endmodule

module Zero_flag (
  output Zero_flag
);

  wire or_1_out;
  wire [7:0] main_1_p1;

  // _8_bit_register_main main_1: pin names not known; wires that end beside it: main_1_p1
  not not_1 (Zero_flag, or_1_out);
  or or_1 (or_1_out, main_1_p1[0], main_1_p1[1], main_1_p1[2], main_1_p1[3], main_1_p1[4], main_1_p1[5], main_1_p1[6], main_1_p1[7]);
endmodule

module Instruction_ko_lagi (
  output DR_Zero
);

  wire [7:0] adder_1_out, main_1_dr_output;

  Bus_main main_1 (.DR_output(main_1_dr_output));  // open: Select, PC_INC, PC_LD, OUTR_LD, S0, TR_INC, TR_LD, IR_INC, IR_LD, A_i_1, DR_INC, A_i_1_2, DR_LD, A_SELECT, ALSU_SELECT, AC_INC, AC_LD, AR_INC, AR_LD, AR_CLR, IR_output, C_in, IR_CLR, RAM_LD, RAM_CLR, DR_CLR, TR_CLR, FGI, AC_CLR, PC_CLR, E, AC_0, AC_7
  Comparator comparator_1 (.a(main_1_dr_output), .b({8{1'b0}}), .eq(DR_Zero));  // open: gt, lt
  Adder adder_1 (.a(main_1_dr_output), .b(8'h1), .out(adder_1_out), .cin(1'b1));  // open: cout
endmodule
