// Logisim project 4-bit_register.circ as structural Verilog: 1 circuit, main circuit main
module main (
  input  [7:0] Bus_Input,
  input  increment,
  input  Load,
  input  CLK,
  input  CLR,
  output [3:0] Z
);

  wire or_1_out;
  wire [3:0] adder_1_out, multiplexer_1_out;

  Adder #(.width(4)) adder_1 (.a(Z), .b(4'b1111), .out(adder_1_out), .cin(1'b0));  // open: cout
  Multiplexer #(.width(4)) multiplexer_1 (
    .in0(Bus_Input[3:0]), .in1(adder_1_out), .out(multiplexer_1_out), .sel(increment));  // open: en
  or or_1 (or_1_out, increment, Load);
  Register #(.width(4)) register_1 (.D(multiplexer_1_out), .en(or_1_out), .Q(Z), .clk(CLK), .clr(CLR));
endmodule
