// Logisim project AR_control.circ as structural Verilog: 1 circuit, main circuit main
module main (
  input  D7,
  input  I,
  input  T3,
  input  AR_LD,
  input  T2,
  input  T0,
  input  R,
  input  D5,
  input  T4,
  output AR_CLR,
  output AR_INR
);

  wire and_1_out, and_2_out, and_3_out, not_1_out;

  not not_1 (not_1_out, R);
  and and_1 (and_1_out, D7, I, T3);
  and and_2 (and_2_out, not_1_out, T2);
  and and_3 (and_3_out, not_1_out, T0);
  and and_4 (AR_CLR, T0, R);
  and and_5 (AR_INR, D5, T4);
  or or_1 (AR_LD, and_1_out, and_2_out, and_3_out);
endmodule
