// Logisim project Bus.circ as structural Verilog: 1 circuit, main circuit main
module main (
  input  [2:0] Source_Select,
  input  S0,
  output E
);

  wire [3:0] AR_4, PC;
  wire [7:0] AC, AR, B, Bus, DR, INPR, IR, main_1_x, OUTR, TR;

  Keyboard keyboard_1 (.data(Bus[6:0]));  // open: clk, re, clr, avail
  _4_bit_register_main u_AR (.Bus_Input(Bus), .Z(AR_4));  // open: S1_S0, increment, Load, CLR, C_out
  _4_bit_register_main u_PC (.Bus_Input(Bus), .Z(PC));  // open: S1_S0, increment, Load, CLR, C_out
  // _8_bit_register_main DR: pin names not known; wires that end beside it: Bus, DR
  // _8_bit_register_main IR: pin names not known; wires that end beside it: Bus, IR
  // _8_bit_register_main TR: pin names not known; wires that end beside it: Bus, TR
  // _8_bit_register_main OUTR: pin names not known; wires that end beside it: Bus, OUTR
  // _8_bit_register_main INPR: pin names not known; wires that end beside it: Bus, INPR
  Multiplexer #(.select(3), .width(8)) multiplexer_1 (
    .in1(AR), .in2({4'b0000, PC}), .in3(DR), .in4(AC), .in5(IR), .in6(TR), .in7(Bus), .out(Bus),
    .sel(Source_Select));  // open: in0, en
  RAM #(.addrWidth(4)) ram_1 (.addr(AR_4), .data(Bus));  // open: sel, clk, ld, clr
  _8_bit_ALSU_main main_1 (.A(AC), .B(B), .E(E), .X(main_1_x));  // open: A_i_1, A_i_1_2, MUX_select, S1_S0, C_in
  Multiplexer #(.width(8)) multiplexer_2 (.in0(INPR), .in1(DR), .out(B), .en(S0));  // open: sel
  // _8_bit_register_main AC: pin names not known; wires that end beside it: main_1_x, AC
  Hex_Digit_Display hex_digit_display_1 (.value(OUTR[3:0]));  // open: dp
  Hex_Digit_Display hex_digit_display_2 (.value(OUTR[7:4]));  // open: dp
  // also tied to GND on the sheet: Bus[7]

  // Other names for the same wires on the sheet: AR_8[3:0] = AR_4; INPUT[7:0] = Bus; RAM[7:0] = Bus
endmodule
